# Fritzing sketch LED_Strip_Breadboard (saved by Fritzing 0.9.3b)
circuit board: 8.46667cm x 5.64444cm
breadboards: 2

parts:
  ROT = Basic FET N-Channel [package="TO220 [THT]"]
  U1 = LuaNode32 / ESP32
  LED_Strip = RGB LED (com. anode, rbg) [package="5 mm [THT]"]
  BLAU = Basic FET N-Channel [package="TO220 [THT]"]
  GRÜN = Basic FET N-Channel [package="TO220 [THT]"]
  U2 = Voltage Regulator - 5V [package="TO220 [THT]"]
  VCC1 = Battery

nets:
  N1: ROT.gate, U1.D13
  N2: ROT.drain, LED_Strip.red_cathode
  GND: ROT.source, U1.GND, BLAU.source, GRÜN.source, U2.GND, VCC1.-
  N3: U1.D14, GRÜN.gate
  N4: U1.D12, BLAU.gate
  N5: U1.Vin, U2.output_voltage
  N6: LED_Strip.common_anode, U2.input_voltage, VCC1.+
  N7: LED_Strip.blue_cathode, BLAU.drain
  N8: LED_Strip.green_cathode, GRÜN.drain

custom parts:
  LuaNode32 / ESP32: ESP32 based LuaNode32
