# Fritzing sketch LED_Strip_Platine (saved by Fritzing 0.9.3b)
circuit board: 8.46667cm x 5.64444cm
stripboards: 1

parts:
  ROT = Basic FET N-Channel [package="TO220 [THT]"]
  U1 = LuaNode32 / ESP32
  LED_Strip = RGB LED (com. anode, rbg) [package="5 mm [THT]"]  # not connected
  BLAU = Basic FET N-Channel [package="TO220 [THT]"]
  GRÜN = Basic FET N-Channel [package="TO220 [THT]"]
  U2 = Voltage Regulator - 5V [package="TO220 [THT]"]  # not connected

nets (from the breadboard view):
  N1: ROT.gate, ROT.drain, ROT.source
  N2: U1.EN, U1.D23, GRÜN.gate
  N3: U1.VP, U1.D22
  N4: U1.VN, U1.TX0
  N5: U1.D34, U1.RX0
  N6: U1.D35, U1.D21, BLAU.gate, BLAU.drain
  N7: U1.D32, U1.D19
  N8: U1.D33, U1.D18
  N9: U1.D25, U1.D5
  N10: U1.D26, U1.TX2
  N11: U1.D27, U1.RX2
  N12: U1.D14, U1.D4
  N13: U1.D12, U1.D2
  N14: U1.D13, U1.D15
  VIN: U1.Vin, U1.3V3
  N15: BLAU.source, GRÜN.source

custom parts:
  LuaNode32 / ESP32: ESP32 based LuaNode32
